# Fritzing sketch esp8266_smartclock (saved by Fritzing 0.9.3b)

parts:
  U1 = NodeMCU V1.0
  Part1 = Matrix LED de 8x8 basada en MAX7219
  RHT1 = Humidity and Temperature Sensor RHT03
  Part2 = Matrix LED de 8x8 basada en MAX7219
  Part3 = Matrix LED de 8x8 basada en MAX7219
  Part4 = Matrix LED de 8x8 basada en MAX7219
  U7 = RF-LINK_TX [package=rf-link_tx]

nets:
  N1: U1.D1, Part1.CLK
  N2: U1.D2, Part1.CS
  N3: U1.D3, Part1.DIN
  N4: U1.D4, U7.DATA
  VCC: U1.3V3, Part1.VCC, RHT1.Vcc, U7.+5V
  GND: U1.GND, Part1.GND#1, RHT1.GND_2, U7.GND
  N5: U1.D5, RHT1.Data-signal
  N6: Part1.VCC(OUT), Part2.VCC
  N7: Part1.GND#6, Part2.GND#1
  N8: Part1.CS(OUT), Part2.CS
  N9: Part1.CLK(OUT), Part2.CLK
  N10: Part1.DOUT, Part2.DIN
  N11: Part2.VCC(OUT), Part3.VCC
  N12: Part2.GND#6, Part3.GND#1
  N13: Part2.CS(OUT), Part3.CS
  N14: Part2.CLK(OUT), Part3.CLK
  N15: Part2.DOUT, Part3.DIN
  N16: Part3.VCC(OUT), Part4.VCC
  N17: Part3.GND#6, Part4.GND
  N18: Part3.CS(OUT), Part4.CS
  N19: Part3.CLK(OUT), Part4.CLK
  N20: Part3.DOUT, Part4.DIN

custom parts:
  NodeMCU V1.0: ESP8266 based NodeMCU
  RF-LINK_TX: Common RF transmitter of the 315.00Mhz varity
